# Fritzing sketch calibration (saved by Fritzing 0.9.3b)

parts:
  Componente1 = Arduino Nano (Rev3.0)
  R3 = TRIMPOT [package=3386u]
  R4 = TRIMPOT [package=3386u]
  R5 = TRIMPOT [package=3386u]
  Componente2 = NRF24L01+ Breakout Board
  S1 = Pushbutton [package="[THT]"]
  R6 = Resistor [tolerance=±5% resistance=220 package=THT]

nets:
  GND: Componente1.GND, Componente1.D2, R3.CCW, R4.CCW, R5.CCW, Componente2.GND, S1.Pin_1, S1.Pin_2
  N1: Componente1.D9, Componente2.CE
  N2: Componente1.D10, Componente2.CS
  N3: Componente1.D11/MOSI, Componente2.MOSI
  N4: Componente1.D12/MISO, Componente2.MISO
  N5: Componente1.5V, R3.CW, R4.CW, R5.CW, R6.Pin_0
  N6: Componente1.A3, R5.WIPER
  N7: Componente1.A2, R4.WIPER
  N8: Componente1.A1, R3.WIPER
  3V3: Componente1.3V3, Componente2.VCC
  N9: Componente1.D13/SCK, Componente2.SCK
