# Fritzing sketch quadcopter (saved by Fritzing 0.9.3b)
circuit board: 8.46667cm x 5.64444cm

parts:
  Componente3 = Arduino Nano (Rev3.0)
  Componente4 = Barometric Pressure Sensor - BMP180 Breakout (GY-68)
  DJI_ESC_30A1 = DJI 30A ESC
  DJI_ESC_30A2 = DJI 30A ESC
  DJI_ESC_30A3 = DJI 30A ESC
  DJI_ESC_30A4 = DJI 30A ESC
  Componente5 = NRF24L01+ Breakout Board
  hc-sr1 = hc-sr04
  GY1 = MPU-6050 Board GY-521 [form="♀ (female)" package=THT]
  LED1 = smd LED [color="Red (633nm)" package="0603 [SMD]"]

nets:
  GND: Componente3.GND, Componente4.GND, DJI_ESC_30A1.GND, DJI_ESC_30A2.GND, DJI_ESC_30A3.GND, DJI_ESC_30A4.GND, Componente5.GND, hc-sr1.GND, GY1.pin2, LED1.cathode
  N1: Componente3.D2, GY1.pin8
  N2: Componente3.D3, DJI_ESC_30A4.DATA
  N3: Componente3.D4, hc-sr1.Trig
  N4: Componente3.D5, DJI_ESC_30A3.DATA
  N5: Componente3.D6, DJI_ESC_30A2.DATA_OUT
  N6: Componente3.D7, LED1.anode
  N7: Componente3.D8, Componente5.CE
  N8: Componente3.D9, DJI_ESC_30A1.DATA, DJI_ESC_30A1.PWR_OUT
  N9: Componente3.D10, Componente5.CS
  N10: Componente3.D11/MOSI, Componente5.MOSI
  N11: Componente3.D12/MISO, Componente5.MISO
  5V: Componente3.5V, hc-sr1.VCC, GY1.pin1
  N12: Componente3.A5, Componente4.SCL, GY1.pin3
  N13: Componente3.A4, Componente4.SDA, GY1.pin4
  N14: Componente3.A3, hc-sr1.Echo
  VCC: Componente3.3V3, Componente4.VCC, Componente5.VCC
  N15: Componente3.D13/SCK, Componente5.SCK

custom parts:
  MPU-6050 Board GY-521: Acelerometro y Giroscopio MPU-6050 Board GY-521
