# Fritzing sketch transmitter (saved by Fritzing 0.9.3b)

parts:
  Componente2 = Arduino Nano (Rev3.0)
  Componente3 = Thumb Joystick
  Componente4 = Thumb Joystick
  Componente5 = NRF24L01+ Breakout Board
  S2 = SWITCH-MOMENTARY-2 [package=tactile_switch_smd-2]
  S3 = SWITCH-MOMENTARY-2 [package=tactile_switch_smd-2]
  R1 = Resistor [tolerance=±5% resistance=220 package="1206 [SMD]"]
  R2 = Resistor [tolerance=±5% resistance=220 package="1206 [SMD]"]
  LED1 = smd LED [color="Red (633nm)" package="0805 [SMD]"]
  LED2 = smd LED [color="Red (633nm)" package="0805 [SMD]"]
  LED3 = smd LED [color="Red (633nm)" package="0603 [SMD]"]
  S4 = SWITCH-MOMENTARY-2 [package=tactile_switch_smd-2]
  R3 = Resistor [tolerance=±5% resistance=220 package="2010 [SMD]"]

nets:
  N1: Componente2.D2, LED3.anode
  N2: Componente2.D3, LED2.anode
  N3: Componente2.D4, LED1.anode
  N4: Componente2.D6, S4.1, R3.Pin_0
  N5: Componente2.D7, S3.1, R2.Pin_0
  N6: Componente2.D8, S2.1, R1.Pin_0
  N7: Componente2.D9, Componente5.CE
  N8: Componente2.D10, Componente5.CS
  N9: Componente2.D11/MOSI, Componente5.MOSI
  N10: Componente2.D12/MISO, Componente5.MISO
  GND: Componente2.GND, Componente4.GND, Componente5.GND, LED1.cathode, LED2.cathode
  VCC: Componente2.5V, Componente3.VCC, Componente4.VCC, S2.2, S3.2, S4.2
  N11: Componente2.A3, Componente3.HORZ
  N12: Componente2.A2, Componente3.VERT
  N13: Componente2.A1, Componente4.HORZ
  N14: Componente2.A0, Componente4.VERT
  3V3: Componente2.3V3, Componente5.VCC
  N15: Componente2.D13/SCK, Componente5.SCK
